# Fritzing sketch Wireless Light Using Nodemcu (saved by Fritzing 0.9.3b)
breadboards: 1

parts:
  U1 = NodeMCU V1.0
  LED1 = LEDs [package=led10mm]
  KY-1 = Keyes Relay [package=THT]
  Power_plug1 = Power plug
  VCC2 = Battery

nets:
  N1: U1.D1, KY-1.signal
  N2: U1.GND, KY-1.ground, VCC2.-
  N3: U1.Vin, KY-1.power, VCC2.+
  N4: LED1.A, Power_plug1.VCC
  N5: LED1.C, KY-1.NO
  N6: KY-1.C, Power_plug1.GND

notes:
  Relay Module
  External Power Supply(220V)
  NodeMCU
  External Power Supply(5V)

custom parts:
  NodeMCU V1.0: ESP8266 based NodeMCU
  LEDs: LEDs Standard schematic elements and footprints for 5mm, 3mm, 1206, and 0603 sized LEDs. 5mm - Spark Fun Electronics SKU : COM-00529 (and others)
  Keyes Relay: The Keyes 5V relay module is suitable for SCM development, home appliance control. It uses a 5V~12V TIL control signal which can control DC / AC signal.
